# Fritzing sketch Ampelschaltung (saved by Fritzing 0.9.5d)
breadboards: 1

parts:
  Bauteil1 = Arduino Uno (Rev3) - ICSP
  LED1 = LED - 5mm [color="Red (633nm)" package="5 mm [THT]"]
  LED2 = LED - 5mm [color="Red (633nm)" package="5 mm [THT]"]
  LED5 = LED - 5mm [color="Green (555nm)" package="5 mm [THT]"]
  LED6 = LED - 5mm [color="Yellow (595nm)" package="5 mm [THT]"]
  LED7 = LED - 5mm [color="Green (555nm)" package="5 mm [THT]"]
  R1 = Resistor [tolerance=±5% resistance=10k package=THT]
  R2 = Resistor [tolerance=±5% resistance=220 package=THT]
  R3 = Resistor [tolerance=±5% resistance=220 package=THT]
  R5 = Resistor [tolerance=±5% resistance=220 package=THT]
  R6 = Resistor [tolerance=±5% resistance=220 package=THT]
  R4 = Resistor [tolerance=±5% resistance=220 package=THT]
  S1 = Pushbutton [package="[THT]"]
  J1 = Piezo Speaker

nets:
  N1: Bauteil1.D8, R2.Pin_0
  N2: Bauteil1.D9_PWM, R6.Pin_0
  N3: Bauteil1.D10_PWM/SS, R5.Pin_0
  N4: Bauteil1.D11_PWM/MOSI, R3.Pin_0
  N5: Bauteil1.D12/MISO, R4.Pin_0
  N6: Bauteil1.D2, R1.Pin_1, S1.Pin_3, S1.Pin_4
  N7: Bauteil1.D7, J1.pin2
  N8: Bauteil1.5V, S1.Pin_1, S1.Pin_2
  N9: Bauteil1.GND, LED1.cathode, LED2.cathode, LED5.cathode, LED6.cathode, LED7.cathode, R1.Pin_0, J1.pin1
  N10: LED1.anode, R4.Pin_1
  N11: LED2.anode, R6.Pin_1
  N12: LED5.anode, R5.Pin_1
  N13: LED6.anode, R3.Pin_1
  N14: LED7.anode, R2.Pin_1
